# Fritzing sketch RevolvingBlueLight_CompactWithHeaderConnectors (saved by Fritzing 0.9.3b)
perfboards: 1

parts:
  LED1 = LEDs [package=led10mm]
  M1 = DC Motor
  Temperature_Sensor = Adafruit BME280 [part_number=BME280]
  Wemos_D1_R1 = WeMos D1 R2
  J3 = female pin header, 2 pins [form="♀ (female)"]  # not connected
  J2 = female pin header, 4 pins [form="♀ (female)"]
  J1 = female pin header, 2 pins [form="♀ (female)"]
  D1 = Upright Rectifier Diode [part_number=1N4007 package="300 mil [THT]"]
  Q2 = NPN-Transistor [V] [part_number=BC547B package="TO92 [THT]"]
  Q1 = NPN-Transistor [V] [part_number=BC547B package="TO92 [THT]"]
  R3 = Resistor [tolerance=±5% resistance=46 package=THT]
  R2 = Resistor [tolerance=±5% resistance=390 package=THT]
  R1 = Resistor [tolerance=±5% resistance=1.1k package=THT]

nets:
  N1: LED1.C, J2.pin4, Q1.C
  N2: LED1.A, J2.pin3, R3.Pin_1
  N3: M1.pin_1, Wemos_D1_R1.5V, J2.pin1, J1.pin2, D1.cathode, R3.Pin_0
  N4: M1.pin_2, J2.pin2, D1.anode, Q2.C
  VIN: Temperature_Sensor.VIN, Wemos_D1_R1.3.3V
  N5: Temperature_Sensor.SCK/SCL, Wemos_D1_R1.D3
  N6: Temperature_Sensor.SDI/SDA, Wemos_D1_R1.D4
  N7: Wemos_D1_R1.D1/TX, R2.Pin_0
  N8: Wemos_D1_R1.D2, R1.Pin_0
  N9: Wemos_D1_R1.GND_3, J1.pin1, Q2.E, Q1.E
  N10: Q2.B, R2.Pin_1
  N11: Q1.B, R1.Pin_1

notes:
  - Perfboard area used: 5x7
  - Mind the upright mounted diode in the second row!
  - The resistors are bridging 3 to 3½
  holes each (fritzing can't visualize this
  better)

custom parts:
  Adafruit BME280: Bosch has stepped up their game with their new BME280 sensor, an environmental sensor with temperature, barometric pressure and humidity! This sensor is great for all sorts of weather/environmental sensing and can even be used in both I2C and SPI! This precision sensor from Bosch is the best low-cost sensing solution for measuring humidity with ±3% accuracy, barometric pressure with ±1 hPa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
  WeMos D1 R2: The D1 R2 is a mini wifi board based on the ESP-8266EX.
  Upright Rectifier Diode: A standard rectifier diode Based on Brendan Howell's work
  NPN-Transistor [V]: A standard NPN-transistor
